// Logisim project dan1.circ as structural Verilog: 19 circuits, main circuit main
module main (
  input  WE_A,
  input  WE_B,
  input  OE_x,
  input  ME,
  input  MWE,
  input  CP,
  input  LD_PC,
  input  PC_OE,
  input  MAR_WE,
  input  MAR_OE,
  input  in_11,
  input  MR,
  input  in_13
);

  wire LEQ;
  wire [7:0] ADDR, controlled_buffer_2_out, dipswitch_1_sw8, dipswitch_2_sw8;

  LED led_1 (.in(ADDR[7]));
  LED led_2 (.in(ADDR[6]));
  LED led_3 (.in(ADDR[4]));
  LED led_4 (.in(ADDR[5]));
  LED led_5 (.in(ADDR[3]));
  DipSwitch dipswitch_1 (
    .sw1(dipswitch_1_sw8[7]), .sw2(dipswitch_1_sw8[6]), .sw3(dipswitch_1_sw8[5]), .sw4(dipswitch_1_sw8[4]),
    .sw5(dipswitch_1_sw8[3]), .sw6(dipswitch_1_sw8[2]), .sw7(dipswitch_1_sw8[1]), .sw8(dipswitch_1_sw8[0]));
  LED led_6 (.in(ADDR[1]));
  LED led_7 (.in(ADDR[2]));
  LED led_8 (.in(ADDR[0]));
  assign ADDR = in_13 ? dipswitch_1_sw8 : 8'bz;  // Controlled_Buffer controlled_buffer_1
  LED led_9 (.in(LEQ));
  DipSwitch dipswitch_2 (
    .sw1(dipswitch_2_sw8[7]), .sw2(dipswitch_2_sw8[6]), .sw3(dipswitch_2_sw8[5]), .sw4(dipswitch_2_sw8[4]),
    .sw5(dipswitch_2_sw8[3]), .sw6(dipswitch_2_sw8[2]), .sw7(dipswitch_2_sw8[1]), .sw8(dipswitch_2_sw8[0]));
  LED led_10 (.in(controlled_buffer_2_out[7]));
  d_PC d_pc_1 (
    .L0(controlled_buffer_2_out[0]), .L1(controlled_buffer_2_out[1]), .L2(controlled_buffer_2_out[2]),
    .L3(controlled_buffer_2_out[3]), .L4(controlled_buffer_2_out[4]), .L5(controlled_buffer_2_out[5]),
    .L6(controlled_buffer_2_out[6]), .L7(controlled_buffer_2_out[7]), .A0(ADDR[0]), .A1(ADDR[1]),
    .A2(ADDR[2]), .A3(ADDR[3]), .A4(ADDR[4]), .A5(ADDR[5]), .A6(ADDR[6]), .A7(ADDR[7]), .CP(CP),
    .LD_4afbc074(LD_PC), .MR_b12a05c5(MR), .OE_b806afc3(PC_OE));
  LED led_11 (.in(controlled_buffer_2_out[3]));
  LED led_12 (.in(controlled_buffer_2_out[6]));
  LED led_13 (.in(controlled_buffer_2_out[4]));
  LED led_14 (.in(controlled_buffer_2_out[5]));
  assign controlled_buffer_2_out = in_11 ? dipswitch_2_sw8 : 8'bz;  // Controlled_Buffer controlled_buffer_2
  d_74374_8bit_register MAR (
    .I0(controlled_buffer_2_out[0]), .I1(controlled_buffer_2_out[1]), .I2(controlled_buffer_2_out[2]),
    .I3(controlled_buffer_2_out[3]), .I4(controlled_buffer_2_out[4]), .I5(controlled_buffer_2_out[5]),
    .I6(controlled_buffer_2_out[6]), .I7(controlled_buffer_2_out[7]), .O0(ADDR[0]), .O1(ADDR[1]),
    .O2(ADDR[2]), .O3(ADDR[3]), .O4(ADDR[4]), .O5(ADDR[5]), .O6(ADDR[6]), .O7(ADDR[7]), .WE_5b31d333(MAR_WE),
    .OE_9ad6e367(MAR_OE));
  LED led_15 (.in(controlled_buffer_2_out[2]));
  LED led_16 (.in(controlled_buffer_2_out[1]));
  LED led_17 (.in(controlled_buffer_2_out[0]));
  d_ALU d_alu_1 (
    .A0(controlled_buffer_2_out[0]), .A1(controlled_buffer_2_out[1]), .A2(controlled_buffer_2_out[2]),
    .A3(controlled_buffer_2_out[3]), .A4(controlled_buffer_2_out[4]), .A5(controlled_buffer_2_out[5]),
    .A6(controlled_buffer_2_out[6]), .A7(controlled_buffer_2_out[7]), .B0(controlled_buffer_2_out[0]),
    .B1(controlled_buffer_2_out[1]), .B2(controlled_buffer_2_out[2]), .B3(controlled_buffer_2_out[3]),
    .B4(controlled_buffer_2_out[4]), .B5(controlled_buffer_2_out[5]), .B6(controlled_buffer_2_out[6]),
    .B7(controlled_buffer_2_out[7]), .OE_b806afc3(OE_x), .WE_A(WE_A), .WE_B(WE_B),
    .O0(controlled_buffer_2_out[0]), .O1(controlled_buffer_2_out[1]), .O2(controlled_buffer_2_out[2]),
    .O3(controlled_buffer_2_out[3]), .O4(controlled_buffer_2_out[4]), .O5(controlled_buffer_2_out[5]),
    .O6(controlled_buffer_2_out[6]), .O7(controlled_buffer_2_out[7]), .leq(LEQ));
  d_RAM_bank_quick d_ram_bank_quick_1 (
    .A(ADDR[0]), .A_2(ADDR[1]), .A_3(ADDR[2]), .A_4(ADDR[3]), .A_5(ADDR[4]), .A_6(ADDR[5]), .A_7(ADDR[6]),
    .A_8(ADDR[7]), .D(controlled_buffer_2_out[0]), .D_2(controlled_buffer_2_out[1]),
    .D_3(controlled_buffer_2_out[2]), .D_4(controlled_buffer_2_out[3]), .D_5(controlled_buffer_2_out[4]),
    .D_6(controlled_buffer_2_out[5]), .D_7(controlled_buffer_2_out[6]), .D_8(controlled_buffer_2_out[7]),
    .ME(ME), .WE(MWE), .S0(controlled_buffer_2_out[0]), .S1(controlled_buffer_2_out[1]),
    .S2(controlled_buffer_2_out[2]), .S3(controlled_buffer_2_out[3]), .S4(controlled_buffer_2_out[4]),
    .S5(controlled_buffer_2_out[5]), .S6(controlled_buffer_2_out[6]), .S7(controlled_buffer_2_out[7]));

  // Other names for the same wires on the sheet: ALU_OE_x = OE_x; ALU_WE_A = WE_A; ALU_WE_B = WE_B

  // Notes on the sheet:
  //   Data Bus
endmodule

module d_74283_4bit_adder (
  input  Cin,
  input  A0,
  input  B0,
  input  A1,
  input  B1,
  input  A2,
  input  B2,
  input  A3,
  input  B3,
  output S0,
  output S1,
  output S2,
  output S3,
  output Cout
);

  wire adder_1_cout, adder_2_cout, adder_3_cout;

  Adder #(.width(1)) adder_1 (.a(A0), .b(B0), .out(S0), .cin(Cin), .cout(adder_1_cout));
  Adder #(.width(1)) adder_2 (.a(A1), .b(B1), .out(S1), .cin(adder_1_cout), .cout(adder_2_cout));
  Adder #(.width(1)) adder_3 (.a(A2), .b(B2), .out(S2), .cin(adder_2_cout), .cout(adder_3_cout));
  Adder #(.width(1)) adder_4 (.a(A3), .b(B3), .out(S3), .cin(adder_3_cout), .cout(Cout));
endmodule

module d_7404_hex_inverter (
  input  in_1,
  input  in_2,
  input  in_3,
  input  in_4,
  input  in_5,
  input  in_6,
  output out_7,
  output out_8,
  output out_9,
  output out_10,
  output out_11,
  output out_12
);

  not not_1 (out_7, in_1);
  not not_2 (out_8, in_2);
  not not_3 (out_9, in_3);
  not not_4 (out_10, in_4);
  not not_5 (out_11, in_5);
  not not_6 (out_12, in_6);
endmodule

module d_7485_4bit_magnitude_comparitor (
  input  Ia_gt_b,
  input  A0,
  input  Ia_lt_b,
  input  B0,
  input  Ia_eq_b,
  input  A1,
  input  B1,
  input  A2,
  input  B2,
  input  A3,
  input  B3,
  output Qa_gt_b,
  output Qa_lt_b,
  output Qa_eq_b
);

  wire and_1_out, and_2_out, and_3_out, and_4_out, and_5_out, and_6_out, and_7_out, and_8_out, and_9_out,
       and_10_out, and_11_out, comparator_1_eq, comparator_1_gt, comparator_1_lt, comparator_2_eq,
       comparator_2_gt, comparator_2_lt, comparator_3_eq, comparator_3_gt, comparator_3_lt, comparator_4_eq,
       comparator_4_gt, comparator_4_lt, or_1_out, or_2_out, or_3_out;

  Comparator #(.width(1)) comparator_1 (
    .a(A0), .b(B0), .gt(comparator_1_gt), .eq(comparator_1_eq), .lt(comparator_1_lt));
  Comparator #(.width(1)) comparator_2 (
    .a(A1), .b(B1), .gt(comparator_2_gt), .eq(comparator_2_eq), .lt(comparator_2_lt));
  Comparator #(.width(1)) comparator_3 (
    .a(A2), .b(B2), .gt(comparator_3_gt), .eq(comparator_3_eq), .lt(comparator_3_lt));
  Comparator #(.width(1)) comparator_4 (
    .a(A3), .b(B3), .gt(comparator_4_gt), .eq(comparator_4_eq), .lt(comparator_4_lt));
  and and_1 (and_1_out, comparator_1_eq, and_4_out);
  and and_2 (and_2_out, comparator_1_lt, and_4_out);
  and and_3 (and_3_out, comparator_1_gt, and_4_out);
  and and_4 (and_4_out, comparator_2_eq, and_7_out);
  and and_5 (and_5_out, comparator_2_lt, and_7_out);
  and and_6 (and_6_out, comparator_2_gt, and_7_out);
  and and_7 (and_7_out, comparator_3_eq, comparator_4_eq);
  and and_8 (and_8_out, comparator_3_lt, comparator_4_eq);
  and and_9 (and_9_out, comparator_4_eq, comparator_3_gt);
  or or_1 (or_1_out, and_2_out, and_8_out, and_5_out, comparator_4_lt);
  or or_2 (or_2_out, and_3_out, and_6_out, and_9_out, comparator_4_gt);
  and and_10 (and_10_out, Ia_gt_b, and_1_out);
  and and_11 (and_11_out, Ia_lt_b, and_1_out);
  or or_3 (or_3_out, Ia_eq_b, and_1_out);
  or or_4 (Qa_lt_b, and_11_out, or_2_out);
  or or_5 (Qa_gt_b, and_10_out, or_1_out);
  and and_12 (Qa_eq_b, or_3_out, ~Qa_gt_b, ~Qa_lt_b);  // AND_Gate
endmodule

module d_ALU (
  input  OE_b806afc3,
  input  WE_A,
  input  A0,
  input  A1,
  input  A2,
  input  A3,
  input  A4,
  input  A5,
  input  A6,
  input  A7,
  input  WE_B,
  input  B0,
  input  B1,
  input  B2,
  input  B3,
  input  B4,
  input  B5,
  input  B6,
  input  B7,
  output O0,
  output O1,
  output O2,
  output O3,
  output O4,
  output O5,
  output O6,
  output O7,
  output leq
);

  wire d_7404_hex_inverter_1_out_7, d_7404_hex_inverter_1_out_8, d_7404_hex_inverter_1_out_9,
       d_7404_hex_inverter_1_out_10, d_7404_hex_inverter_2_out_7, d_7404_hex_inverter_2_out_8,
       d_7404_hex_inverter_2_out_9, d_7404_hex_inverter_2_out_10, d_7485_4bit_magnitude_comparitor_1_qa_eq_b,
       d_7485_4bit_magnitude_comparitor_1_qa_gt_b, d_7485_4bit_magnitude_comparitor_1_qa_lt_b,
       d_7485_4bit_magnitude_comparitor_2_qa_eq_b, d_74283_4bit_adder_1_cout, d_74283_4bit_adder_1_s0,
       d_74283_4bit_adder_1_s1, d_74283_4bit_adder_1_s2, d_74283_4bit_adder_1_s3, d_74283_4bit_adder_2_s0,
       d_74283_4bit_adder_2_s1, d_74283_4bit_adder_2_s2, d_74283_4bit_adder_2_s3, d_74374_8bit_register_1_o0,
       d_74374_8bit_register_1_o1, d_74374_8bit_register_1_o2, d_74374_8bit_register_1_o3,
       d_74374_8bit_register_1_o4, d_74374_8bit_register_1_o5, d_74374_8bit_register_1_o6,
       d_74374_8bit_register_1_o7, d_74374_8bit_register_2_o0, d_74374_8bit_register_2_o1,
       d_74374_8bit_register_2_o2, d_74374_8bit_register_2_o3, d_74374_8bit_register_2_o4,
       d_74374_8bit_register_2_o5, d_74374_8bit_register_2_o6, d_74374_8bit_register_2_o7, or_1_out;

  d_74374_8bit_register d_74374_8bit_register_1 (
    .I0(A0), .I1(A1), .I2(A2), .I3(A3), .I4(A4), .I5(A5), .I6(A6), .I7(A7), .O0(d_74374_8bit_register_1_o0),
    .O1(d_74374_8bit_register_1_o1), .O2(d_74374_8bit_register_1_o2), .O3(d_74374_8bit_register_1_o3),
    .O4(d_74374_8bit_register_1_o4), .O5(d_74374_8bit_register_1_o5), .O6(d_74374_8bit_register_1_o6),
    .O7(d_74374_8bit_register_1_o7), .WE_5b31d333(WE_A), .OE_9ad6e367(1'b0));
  d_74374_8bit_register d_74374_8bit_register_2 (
    .I0(B0), .I1(B1), .I2(B2), .I3(B3), .I4(B4), .I5(B5), .I6(B6), .I7(B7), .O0(d_74374_8bit_register_2_o0),
    .O1(d_74374_8bit_register_2_o1), .O2(d_74374_8bit_register_2_o2), .O3(d_74374_8bit_register_2_o3),
    .O4(d_74374_8bit_register_2_o4), .O5(d_74374_8bit_register_2_o5), .O6(d_74374_8bit_register_2_o6),
    .O7(d_74374_8bit_register_2_o7), .WE_5b31d333(WE_B), .OE_9ad6e367(1'b0));
  d_7404_hex_inverter d_7404_hex_inverter_1 (
    .in_1(d_74374_8bit_register_1_o0), .in_2(d_74374_8bit_register_1_o1), .in_3(d_74374_8bit_register_1_o2),
    .in_4(d_74374_8bit_register_1_o3), .out_7(d_7404_hex_inverter_1_out_7),
    .out_8(d_7404_hex_inverter_1_out_8), .out_9(d_7404_hex_inverter_1_out_9),
    .out_10(d_7404_hex_inverter_1_out_10));  // open: in_5, in_6, out_11, out_12
  d_7404_hex_inverter d_7404_hex_inverter_2 (
    .in_1(d_74374_8bit_register_1_o4), .in_2(d_74374_8bit_register_1_o5), .in_3(d_74374_8bit_register_1_o6),
    .in_4(d_74374_8bit_register_1_o7), .out_7(d_7404_hex_inverter_2_out_7),
    .out_8(d_7404_hex_inverter_2_out_8), .out_9(d_7404_hex_inverter_2_out_9),
    .out_10(d_7404_hex_inverter_2_out_10));  // open: in_5, in_6, out_11, out_12
  d_74283_4bit_adder d_74283_4bit_adder_1 (
    .A0(d_7404_hex_inverter_1_out_7), .B0(d_74374_8bit_register_2_o0), .A1(d_7404_hex_inverter_1_out_8),
    .B1(d_74374_8bit_register_2_o1), .A2(d_7404_hex_inverter_1_out_9), .B2(d_74374_8bit_register_2_o2),
    .A3(d_7404_hex_inverter_1_out_10), .B3(d_74374_8bit_register_2_o3), .S0(d_74283_4bit_adder_1_s0),
    .S1(d_74283_4bit_adder_1_s1), .S2(d_74283_4bit_adder_1_s2), .S3(d_74283_4bit_adder_1_s3), .Cin(1'b1),
    .Cout(d_74283_4bit_adder_1_cout));
  d_74283_4bit_adder d_74283_4bit_adder_2 (
    .A0(d_7404_hex_inverter_2_out_7), .B0(d_74374_8bit_register_2_o4), .A1(d_7404_hex_inverter_2_out_8),
    .B1(d_74374_8bit_register_2_o5), .A2(d_7404_hex_inverter_2_out_9), .B2(d_74374_8bit_register_2_o6),
    .A3(d_7404_hex_inverter_2_out_10), .B3(d_74374_8bit_register_2_o7), .S0(d_74283_4bit_adder_2_s0),
    .S1(d_74283_4bit_adder_2_s1), .S2(d_74283_4bit_adder_2_s2), .S3(d_74283_4bit_adder_2_s3),
    .Cin(d_74283_4bit_adder_1_cout));  // open: Cout
  d_7485_4bit_magnitude_comparitor d_7485_4bit_magnitude_comparitor_1 (
    .A0(d_74283_4bit_adder_1_s0), .B0(1'b0), .A1(d_74283_4bit_adder_1_s1), .B1(1'b0),
    .A2(d_74283_4bit_adder_1_s2), .B2(1'b0), .A3(d_74283_4bit_adder_1_s3), .B3(1'b0),
    .Qa_gt_b(d_7485_4bit_magnitude_comparitor_1_qa_gt_b),
    .Qa_lt_b(d_7485_4bit_magnitude_comparitor_1_qa_lt_b),
    .Qa_eq_b(d_7485_4bit_magnitude_comparitor_1_qa_eq_b), .Ia_gt_b(1'b0), .Ia_lt_b(1'b0), .Ia_eq_b(1'b0));
  d_7485_4bit_magnitude_comparitor d_7485_4bit_magnitude_comparitor_2 (
    .A0(d_74283_4bit_adder_2_s0), .B0(1'b0), .A1(d_74283_4bit_adder_2_s1), .B1(1'b0),
    .A2(d_74283_4bit_adder_2_s2), .B2(1'b0), .A3(d_74283_4bit_adder_2_s3), .B3(1'b0),
    .Qa_eq_b(d_7485_4bit_magnitude_comparitor_2_qa_eq_b),
    .Ia_gt_b(d_7485_4bit_magnitude_comparitor_1_qa_gt_b),
    .Ia_lt_b(d_7485_4bit_magnitude_comparitor_1_qa_lt_b), .Ia_eq_b(d_7485_4bit_magnitude_comparitor_1_qa_eq_b));  // open: Qa_gt_b, Qa_lt_b
  or or_1 (or_1_out, d_74283_4bit_adder_2_s3, d_7485_4bit_magnitude_comparitor_2_qa_eq_b);
  d_74125_4bit_buffer d_74125_4bit_buffer_1 (
    .in_2(or_1_out), .out_6(leq), .G_a0c2a5f7(OE_b806afc3));  // open: in_3, in_4, in_5, out_7, out_8, out_9
  d_74244_8bit_buffer d_74244_8bit_buffer_1 (
    .in_3(d_74283_4bit_adder_1_s0), .in_4(d_74283_4bit_adder_1_s1), .in_5(d_74283_4bit_adder_1_s2),
    .in_6(d_74283_4bit_adder_1_s3), .in_7(d_74283_4bit_adder_2_s0), .in_8(d_74283_4bit_adder_2_s1),
    .in_9(d_74283_4bit_adder_2_s2), .in_10(d_74283_4bit_adder_2_s3), .out_11(O0), .out_12(O1), .out_13(O2),
    .out_14(O3), .out_15(O4), .out_16(O5), .out_17(O6), .out_18(O7), .G1_e9a0e9ff(OE_b806afc3),
    .G2_cb29eafa(OE_b806afc3));

  // Notes on the sheet:
  //   Input_a
endmodule

module d_74173_quad_d_flipflop (
  input  E_1,
  input  E_2,
  input  CP,
  input  MR,
  input  OE_1,
  input  OE_2,
  input  D0,
  input  D1,
  input  D2,
  input  D3,
  output Q0,
  output Q1,
  output Q2,
  output Q3
);

  wire and_1_out, and_2_out;
  wire [3:0] register_1_q;

  and and_1 (and_1_out, ~E_1, ~E_2);  // AND_Gate
  Register #(.width(4)) register_1 (.D({D3, D2, D1, D0}), .en(and_1_out), .clk(CP), .Q(register_1_q));  // open: clr
  and and_2 (and_2_out, ~OE_1, ~OE_2);  // AND_Gate
  assign Q0 = and_2_out ? register_1_q[0] : 1'bz;  // Controlled_Buffer controlled_buffer_1
  assign Q1 = and_2_out ? register_1_q[1] : 1'bz;  // Controlled_Buffer controlled_buffer_2
  assign Q2 = and_2_out ? register_1_q[2] : 1'bz;  // Controlled_Buffer controlled_buffer_3
  assign Q3 = and_2_out ? register_1_q[3] : 1'bz;  // Controlled_Buffer controlled_buffer_4
endmodule

module d_74374_8bit_register (
  input  WE_5b31d333,
  input  OE_9ad6e367,
  input  I0,
  input  I1,
  input  I2,
  input  I3,
  input  I4,
  input  I5,
  input  I6,
  input  I7,
  output O0,
  output O1,
  output O2,
  output O3,
  output O4,
  output O5,
  output O6,
  output O7
);

  d_74173_quad_d_flipflop d_74173_quad_d_flipflop_1 (
    .D0(I0), .D1(I1), .D2(I2), .D3(I3), .Q0(O0), .Q1(O1), .Q2(O2), .Q3(O3), .E_1(WE_5b31d333),
    .E_2(WE_5b31d333), .CP(WE_5b31d333), .MR(1'b0), .OE_1(OE_9ad6e367), .OE_2(OE_9ad6e367));
  d_74173_quad_d_flipflop d_74173_quad_d_flipflop_2 (
    .D0(I4), .D1(I5), .D2(I6), .D3(I7), .Q0(O4), .Q1(O5), .Q2(O6), .Q3(O7), .E_1(WE_5b31d333),
    .E_2(WE_5b31d333), .CP(WE_5b31d333), .MR(1'b0), .OE_1(OE_9ad6e367), .OE_2(OE_9ad6e367));
  Controlled_Buffer controlled_buffer_1 ();  // open: in, out, en
endmodule

module d_74161_4bit_counter (
  input  CP,
  input  CI,
  input  LD_4afbc074,
  input  MR_b12a05c5,
  input  in_5,
  input  in_6,
  input  in_7,
  input  in_8,
  output out_9,
  output out_10,
  output out_11,
  output out_12,
  output CO
);

  wire not_1_out, not_2_out;

  not not_1 (not_1_out, LD_4afbc074);
  not not_2 (not_2_out, MR_b12a05c5);
  Counter #(.width(4), .max('hf)) counter_1 (
    .clr(not_2_out), .load(not_1_out), .up(1'b1), .count(CI), .clk(CP), .D({in_8, in_7, in_6, in_5}),
    .carry(CO), .Q({out_12, out_11, out_10, out_9}));
endmodule

module d_PC (
  input  CP,
  input  LD_4afbc074,
  input  MR_b12a05c5,
  input  OE_b806afc3,
  input  L0,
  input  L1,
  input  L2,
  input  L3,
  input  L4,
  input  L5,
  input  L6,
  input  L7,
  output A0,
  output A1,
  output A2,
  output A3,
  output A4,
  output A5,
  output A6,
  output A7
);

  wire d_74161_4bit_counter_1_co, d_74161_4bit_counter_1_out_9, d_74161_4bit_counter_1_out_10,
       d_74161_4bit_counter_1_out_11, d_74161_4bit_counter_1_out_12, d_74161_4bit_counter_2_out_9,
       d_74161_4bit_counter_2_out_10, d_74161_4bit_counter_2_out_11, d_74161_4bit_counter_2_out_12;

  d_74161_4bit_counter d_74161_4bit_counter_1 (
    .in_5(L0), .in_6(L1), .in_7(L2), .in_8(L3), .out_9(d_74161_4bit_counter_1_out_9),
    .out_10(d_74161_4bit_counter_1_out_10), .out_11(d_74161_4bit_counter_1_out_11),
    .out_12(d_74161_4bit_counter_1_out_12), .CP(CP), .CI(1'b1), .LD_4afbc074(LD_4afbc074),
    .MR_b12a05c5(MR_b12a05c5), .CO(d_74161_4bit_counter_1_co));
  d_74161_4bit_counter d_74161_4bit_counter_2 (
    .in_5(L4), .in_6(L5), .in_7(L6), .in_8(L7), .out_9(d_74161_4bit_counter_2_out_9),
    .out_10(d_74161_4bit_counter_2_out_10), .out_11(d_74161_4bit_counter_2_out_11),
    .out_12(d_74161_4bit_counter_2_out_12), .CP(CP), .CI(d_74161_4bit_counter_1_co),
    .LD_4afbc074(LD_4afbc074), .MR_b12a05c5(MR_b12a05c5));  // open: CO
  d_74244_8bit_buffer d_74244_8bit_buffer_1 (
    .in_3(d_74161_4bit_counter_1_out_9), .in_4(d_74161_4bit_counter_1_out_10),
    .in_5(d_74161_4bit_counter_1_out_11), .in_6(d_74161_4bit_counter_1_out_12),
    .in_7(d_74161_4bit_counter_2_out_9), .in_8(d_74161_4bit_counter_2_out_10),
    .in_9(d_74161_4bit_counter_2_out_11), .in_10(d_74161_4bit_counter_2_out_12), .out_11(A0), .out_12(A1),
    .out_13(A2), .out_14(A3), .out_15(A4), .out_16(A5), .out_17(A6), .out_18(A7), .G1_e9a0e9ff(OE_b806afc3),
    .G2_cb29eafa(OE_b806afc3));
endmodule

module d_74244_8bit_buffer (
  input  G1_e9a0e9ff,
  input  G2_cb29eafa,
  input  in_3,
  input  in_4,
  input  in_5,
  input  in_6,
  input  in_7,
  input  in_8,
  input  in_9,
  input  in_10,
  output out_11,
  output out_12,
  output out_13,
  output out_14,
  output out_15,
  output out_16,
  output out_17,
  output out_18
);

  wire not_1_out, not_2_out;

  assign out_11 = not_2_out ? in_3 : 1'bz;  // Controlled_Buffer controlled_buffer_1
  assign out_12 = not_2_out ? in_4 : 1'bz;  // Controlled_Buffer controlled_buffer_2
  assign out_13 = not_2_out ? in_5 : 1'bz;  // Controlled_Buffer controlled_buffer_3
  assign out_14 = not_2_out ? in_6 : 1'bz;  // Controlled_Buffer controlled_buffer_4
  assign out_15 = not_1_out ? in_7 : 1'bz;  // Controlled_Buffer controlled_buffer_5
  assign out_16 = not_1_out ? in_8 : 1'bz;  // Controlled_Buffer controlled_buffer_6
  assign out_17 = not_1_out ? in_9 : 1'bz;  // Controlled_Buffer controlled_buffer_7
  assign out_18 = not_1_out ? in_10 : 1'bz;  // Controlled_Buffer controlled_buffer_8
  not not_1 (not_1_out, G2_cb29eafa);
  not not_2 (not_2_out, G1_e9a0e9ff);
endmodule

module d_74125_4bit_buffer (
  input  G_a0c2a5f7,
  input  in_2,
  input  in_3,
  input  in_4,
  input  in_5,
  output out_6,
  output out_7,
  output out_8,
  output out_9
);

  wire not_1_out;

  assign out_6 = not_1_out ? in_2 : 1'bz;  // Controlled_Buffer controlled_buffer_1
  assign out_7 = not_1_out ? in_3 : 1'bz;  // Controlled_Buffer controlled_buffer_2
  assign out_8 = not_1_out ? in_4 : 1'bz;  // Controlled_Buffer controlled_buffer_3
  assign out_9 = not_1_out ? in_5 : 1'bz;  // Controlled_Buffer controlled_buffer_4
  not not_1 (not_1_out, G_a0c2a5f7);
endmodule

module d_74189_RAM (
  input  ME,
  input  WE,
  input  A0,
  input  A1,
  input  A2,
  input  A3,
  input  D0,
  input  D1,
  input  D2,
  input  D3,
  output S0,
  output S1,
  output S2,
  output S3
);

  wire and_1_out, and_2_out;
  wire [3:0] ram_1_dout;

  RAM #(.addrWidth(4), .dataWidth(4), .trigger("high"), .databus("bibus")) ram_1 (
    .addr({A3, A2, A1, A0}), .we(and_2_out), .oe(and_1_out), .din({D3, D2, D1, D0}), .dout(ram_1_dout));
  and and_1 (and_1_out, ~ME, WE);  // AND_Gate
  and and_2 (and_2_out, ~ME, ~WE);  // AND_Gate
  assign {S3, S2, S1, S0} = and_1_out ? ~ram_1_dout : 4'bz;  // Controlled_Inverter controlled_inverter_1
endmodule

module d_74154_4_16_decoder (
  input  G1_26749ebb,
  input  G2_f52fa05c,
  input  A,
  input  B,
  input  C,
  input  D,
  output out_7,
  output out_8,
  output out_9,
  output out_10,
  output out_11,
  output out_12,
  output out_13,
  output out_14,
  output out_15,
  output out_16,
  output out_17,
  output out_18,
  output out_19,
  output out_20,
  output out_21,
  output out_22
);

  wire and_1_out;

  and and_1 (and_1_out, ~G1_26749ebb, ~G2_f52fa05c);  // AND_Gate
  Decoder #(.select(4)) decoder_1 (
    .out0(out_7), .out1(out_8), .out2(out_9), .out3(out_10), .out4(out_11), .out5(out_12), .out6(out_13),
    .out7(out_14), .out8(out_15), .out9(out_16), .out10(out_17), .out11(out_18), .out12(out_19),
    .out13(out_20), .out14(out_21), .out15(out_22), .sel({D, C, B, A}), .en(and_1_out));
endmodule

module d_RAM_bank_74189 (
  input  ME,
  input  WE,
  input  D0,
  input  D1,
  input  D2,
  input  D3,
  input  D4,
  input  D5,
  input  D6,
  input  D7,
  input  A0,
  input  A1,
  input  A2,
  input  A3,
  input  A4,
  input  A5,
  input  A6,
  input  A7,
  output S0,
  output S1,
  output S2,
  output S3,
  output S4,
  output S5,
  output S6,
  output S7
);

  wire D0_t, D1_t, D2_t, D3_t, D4_t, D5_t, D6_t, D7_t, ME0, ME1, ME2, ME3, ME4, ME5, ME6, ME7, ME8, ME9,
       ME10, ME11, ME12, ME13, ME14;

  d_7404_hex_inverter d_7404_hex_inverter_1 (
    .in_1(D0), .in_2(D1), .in_3(D2), .in_4(D3), .out_7(D0_t), .out_8(D1_t), .out_9(D2_t), .out_10(D3_t));  // open: in_5, in_6, out_11, out_12
  d_7404_hex_inverter d_7404_hex_inverter_2 (
    .in_1(D4), .in_2(D5), .in_3(D6), .in_4(D7), .out_7(D4_t), .out_8(D5_t), .out_9(D6_t), .out_10(D7_t));  // open: in_5, in_6, out_11, out_12
  d_74138_3_8_decoder d_74138_3_8_decoder_1 (
    .A0(A4), .A1(A5), .A2(A6), .out_7(ME0), .out_8(ME1), .out_9(ME2), .out_10(ME3), .out_11(ME4),
    .out_12(ME5), .out_13(ME6), .out_14(ME7), .E1_48a29ffd(A7), .E2_fb63e4fe(ME), .E3(1'b1));
  d_74138_3_8_decoder d_74138_3_8_decoder_2 (
    .A0(A4), .A1(A5), .A2(A6), .out_7(ME8), .out_8(ME9), .out_9(ME10), .out_10(ME11), .out_11(ME12),
    .out_12(ME13), .out_13(ME14), .E1_48a29ffd(1'b0), .E2_fb63e4fe(ME), .E3(A7));  // open: out_14
  d_74189_RAM d_74189_ram_1 (
    .A0(A0), .A1(A1), .A2(A2), .A3(A3), .D0(D0_t), .D1(D1_t), .D2(D2_t), .D3(D3_t), .S0(S0), .S1(S1),
    .S2(S2), .S3(S3), .ME(ME0), .WE(WE));
  d_74189_RAM d_74189_ram_2 (
    .A0(A0), .A1(A1), .A2(A2), .A3(A3), .D0(D0_t), .D1(D1_t), .D2(D2_t), .D3(D3_t), .S0(S0), .S1(S1),
    .S2(S2), .S3(S3), .ME(ME1), .WE(WE));
  d_74189_RAM d_74189_ram_3 (
    .A0(A0), .A1(A1), .A2(A2), .A3(A3), .D0(D0_t), .D1(D1_t), .D2(D2_t), .D3(D3_t), .S0(S0), .S1(S1),
    .S2(S2), .S3(S3), .ME(ME2), .WE(WE));
  d_74189_RAM d_74189_ram_4 (
    .A0(A0), .A1(A1), .A2(A2), .A3(A3), .D0(D0_t), .D1(D1_t), .D2(D2_t), .D3(D3_t), .S0(S0), .S1(S1),
    .S2(S2), .S3(S3), .ME(ME3), .WE(WE));
  d_74189_RAM d_74189_ram_5 (
    .A0(A0), .A1(A1), .A2(A2), .A3(A3), .D0(D4_t), .D1(D5_t), .D2(D6_t), .D3(D7_t), .S0(S4), .S1(S5),
    .S2(S6), .S3(S7), .ME(ME0), .WE(WE));
  d_74189_RAM d_74189_ram_6 (
    .A0(A0), .A1(A1), .A2(A2), .A3(A3), .D0(D4_t), .D1(D5_t), .D2(D6_t), .D3(D7_t), .S0(S4), .S1(S5),
    .S2(S6), .S3(S7), .ME(ME1), .WE(WE));
  d_74189_RAM d_74189_ram_7 (
    .A0(A0), .A1(A1), .A2(A2), .A3(A3), .D0(D4_t), .D1(D5_t), .D2(D6_t), .D3(D7_t), .S0(S4), .S1(S5),
    .S2(S6), .S3(S7), .ME(ME2), .WE(WE));
  d_74189_RAM d_74189_ram_8 (
    .A0(A0), .A1(A1), .A2(A2), .A3(A3), .D0(D4_t), .D1(D5_t), .D2(D6_t), .D3(D7_t), .S0(S4), .S1(S5),
    .S2(S6), .S3(S7), .ME(ME3), .WE(WE));
  d_74189_RAM d_74189_ram_9 (
    .A0(A0), .A1(A1), .A2(A2), .A3(A3), .D0(D0_t), .D1(D1_t), .D2(D2_t), .D3(D3_t), .S0(S0), .S1(S1),
    .S2(S2), .S3(S3), .ME(ME4), .WE(WE));
  d_74189_RAM d_74189_ram_10 (
    .A0(A0), .A1(A1), .A2(A2), .A3(A3), .D0(D0_t), .D1(D1_t), .D2(D2_t), .D3(D3_t), .S0(S0), .S1(S1),
    .S2(S2), .S3(S3), .ME(ME5), .WE(WE));
  d_74189_RAM d_74189_ram_11 (
    .A0(A0), .A1(A1), .A2(A2), .A3(A3), .D0(D0_t), .D1(D1_t), .D2(D2_t), .D3(D3_t), .S0(S0), .S1(S1),
    .S2(S2), .S3(S3), .ME(ME6), .WE(WE));
  d_74189_RAM d_74189_ram_12 (
    .A0(A0), .A1(A1), .A2(A2), .A3(A3), .D0(D0_t), .D1(D1_t), .D2(D2_t), .D3(D3_t), .S0(S0), .S1(S1),
    .S2(S2), .S3(S3), .ME(ME7), .WE(WE));
  d_74189_RAM d_74189_ram_13 (
    .A0(A0), .A1(A1), .A2(A2), .A3(A3), .D0(D4_t), .D1(D5_t), .D2(D6_t), .D3(D7_t), .S0(S4), .S1(S5),
    .S2(S6), .S3(S7), .ME(ME4), .WE(WE));
  d_74189_RAM d_74189_ram_14 (
    .A0(A0), .A1(A1), .A2(A2), .A3(A3), .D0(D4_t), .D1(D5_t), .D2(D6_t), .D3(D7_t), .S0(S4), .S1(S5),
    .S2(S6), .S3(S7), .ME(ME5), .WE(WE));
  d_74189_RAM d_74189_ram_15 (
    .A0(A0), .A1(A1), .A2(A2), .A3(A3), .D0(D4_t), .D1(D5_t), .D2(D6_t), .D3(D7_t), .S0(S4), .S1(S5),
    .S2(S6), .S3(S7), .ME(ME6), .WE(WE));
  d_74189_RAM d_74189_ram_16 (
    .A0(A0), .A1(A1), .A2(A2), .A3(A3), .D0(D4_t), .D1(D5_t), .D2(D6_t), .D3(D7_t), .S0(S4), .S1(S5),
    .S2(S6), .S3(S7), .ME(ME7), .WE(WE));
  d_74189_RAM d_74189_ram_17 (
    .A0(A0), .A1(A1), .A2(A2), .A3(A3), .D0(D0_t), .D1(D1_t), .D2(D2_t), .D3(D3_t), .S0(S0), .S1(S1),
    .S2(S2), .S3(S3), .ME(ME8), .WE(WE));
  d_74189_RAM d_74189_ram_18 (
    .A0(A0), .A1(A1), .A2(A2), .A3(A3), .D0(D0_t), .D1(D1_t), .D2(D2_t), .D3(D3_t), .S0(S0), .S1(S1),
    .S2(S2), .S3(S3), .ME(ME9), .WE(WE));
  d_74189_RAM d_74189_ram_19 (
    .A0(A0), .A1(A1), .A2(A2), .A3(A3), .D0(D0_t), .D1(D1_t), .D2(D2_t), .D3(D3_t), .S0(S0), .S1(S1),
    .S2(S2), .S3(S3), .ME(ME10), .WE(WE));
  d_74189_RAM d_74189_ram_20 (
    .A0(A0), .A1(A1), .A2(A2), .A3(A3), .D0(D0_t), .D1(D1_t), .D2(D2_t), .D3(D3_t), .S0(S0), .S1(S1),
    .S2(S2), .S3(S3), .ME(ME11), .WE(WE));
  d_74189_RAM d_74189_ram_21 (
    .A0(A0), .A1(A1), .A2(A2), .A3(A3), .D0(D4_t), .D1(D5_t), .D2(D6_t), .D3(D7_t), .S0(S4), .S1(S5),
    .S2(S6), .S3(S7), .ME(ME8), .WE(WE));
  d_74189_RAM d_74189_ram_22 (
    .A0(A0), .A1(A1), .A2(A2), .A3(A3), .D0(D4_t), .D1(D5_t), .D2(D6_t), .D3(D7_t), .S0(S4), .S1(S5),
    .S2(S6), .S3(S7), .ME(ME9), .WE(WE));
  d_74189_RAM d_74189_ram_23 (
    .A0(A0), .A1(A1), .A2(A2), .A3(A3), .D0(D4_t), .D1(D5_t), .D2(D6_t), .D3(D7_t), .S0(S4), .S1(S5),
    .S2(S6), .S3(S7), .ME(ME10), .WE(WE));
  d_74189_RAM d_74189_ram_24 (
    .A0(A0), .A1(A1), .A2(A2), .A3(A3), .D0(D4_t), .D1(D5_t), .D2(D6_t), .D3(D7_t), .S0(S4), .S1(S5),
    .S2(S6), .S3(S7), .ME(ME11), .WE(WE));
  d_74189_RAM d_74189_ram_25 (
    .A0(A0), .A1(A1), .A2(A2), .A3(A3), .D0(D0_t), .D1(D1_t), .D2(D2_t), .D3(D3_t), .S0(S0), .S1(S1),
    .S2(S2), .S3(S3), .ME(ME12), .WE(WE));
  d_74189_RAM d_74189_ram_26 (
    .A0(A0), .A1(A1), .A2(A2), .A3(A3), .D0(D0_t), .D1(D1_t), .D2(D2_t), .D3(D3_t), .S0(S0), .S1(S1),
    .S2(S2), .S3(S3), .ME(ME13), .WE(WE));
  d_74189_RAM d_74189_ram_27 (
    .A0(A0), .A1(A1), .A2(A2), .A3(A3), .D0(D0_t), .D1(D1_t), .D2(D2_t), .D3(D3_t), .S0(S0), .S1(S1),
    .S2(S2), .S3(S3), .ME(ME14), .WE(WE));
  d_74189_RAM d_74189_ram_28 (
    .A0(A0), .A1(A1), .A2(A2), .A3(A3), .D0(D0_t), .D1(D1_t), .D2(D2_t), .D3(D3_t), .S0(S0), .S1(S1),
    .S2(S2), .S3(S3), .ME(1'b1), .WE(WE));
  d_74189_RAM d_74189_ram_29 (
    .A0(A0), .A1(A1), .A2(A2), .A3(A3), .D0(D4_t), .D1(D5_t), .D2(D6_t), .D3(D7_t), .S0(S4), .S1(S5),
    .S2(S6), .S3(S7), .ME(ME12), .WE(WE));
  d_74189_RAM d_74189_ram_30 (
    .A0(A0), .A1(A1), .A2(A2), .A3(A3), .D0(D4_t), .D1(D5_t), .D2(D6_t), .D3(D7_t), .S0(S4), .S1(S5),
    .S2(S6), .S3(S7), .ME(ME13), .WE(WE));
  d_74189_RAM d_74189_ram_31 (
    .A0(A0), .A1(A1), .A2(A2), .A3(A3), .D0(D4_t), .D1(D5_t), .D2(D6_t), .D3(D7_t), .S0(S4), .S1(S5),
    .S2(S6), .S3(S7), .ME(ME14), .WE(WE));
  d_74189_RAM d_74189_ram_32 (
    .A0(A0), .A1(A1), .A2(A2), .A3(A3), .D0(D4_t), .D1(D5_t), .D2(D6_t), .D3(D7_t), .S0(S4), .S1(S5),
    .S2(S6), .S3(S7), .ME(1'b1), .WE(WE));
endmodule

module d_74138_3_8_decoder (
  input  E1_48a29ffd,
  input  E2_fb63e4fe,
  input  E3,
  input  A0,
  input  A1,
  input  A2,
  output out_7,
  output out_8,
  output out_9,
  output out_10,
  output out_11,
  output out_12,
  output out_13,
  output out_14
);

  wire and_1_out, decoder_1_out0, decoder_1_out1, decoder_1_out2, decoder_1_out3, decoder_1_out4,
       decoder_1_out5, decoder_1_out6, decoder_1_out7;

  and and_1 (and_1_out, ~E1_48a29ffd, ~E2_fb63e4fe, E3);  // AND_Gate
  Decoder #(.select(3)) decoder_1 (
    .out0(decoder_1_out0), .out1(decoder_1_out1), .out2(decoder_1_out2), .out3(decoder_1_out3),
    .out4(decoder_1_out4), .out5(decoder_1_out5), .out6(decoder_1_out6), .out7(decoder_1_out7),
    .sel({A2, A1, A0}), .en(and_1_out));
  not not_1 (out_7, decoder_1_out0);
  not not_2 (out_8, decoder_1_out1);
  not not_3 (out_9, decoder_1_out2);
  not not_4 (out_10, decoder_1_out3);
  not not_5 (out_11, decoder_1_out4);
  not not_6 (out_12, decoder_1_out5);
  not not_7 (out_13, decoder_1_out6);
  not not_8 (out_14, decoder_1_out7);
endmodule

module d_RAM_bank_quick (
  input  ME,
  input  WE,
  input  A,
  input  A_2,
  input  A_3,
  input  A_4,
  input  A_5,
  input  A_6,
  input  A_7,
  input  A_8,
  input  D,
  input  D_2,
  input  D_3,
  input  D_4,
  input  D_5,
  input  D_6,
  input  D_7,
  input  D_8,
  output S0,
  output S1,
  output S2,
  output S3,
  output S4,
  output S5,
  output S6,
  output S7
);

  wire and_1_out, and_3_out, d_7420_2x4_input_nand_1_y1, ME_t, WE_t;

  d_7420_2x4_input_NAND d_7420_2x4_input_nand_1 (
    .A1(A_5), .B1(A_6), .C1(A_7), .D1(A_8), .Y1(d_7420_2x4_input_nand_1_y1));  // open: A2, B2, C2, D2, Y2
  RAM #(.trigger("high"), .databus("bibus")) RAM (
    .addr({A_8, A_7, A_6, A_5, A_4, A_3, A_2, A}), .we(WE_t), .oe(ME_t),
    .din({D_8, D_7, D_6, D_5, D_4, D_3, D_2, D}), .dout({S7, S6, S5, S4, S3, S2, S1, S0}));
  and and_1 (and_1_out, ~ME, WE);  // AND_Gate
  and and_2 (ME_t, and_1_out, d_7420_2x4_input_nand_1_y1);
  and and_3 (and_3_out, ~ME, ~WE);  // AND_Gate
  and and_4 (WE_t, and_3_out, d_7420_2x4_input_nand_1_y1);
endmodule

module d_7411_3x3_input_AND (
  input  A1,
  input  B1,
  input  C1,
  input  A2,
  input  B2,
  input  C2,
  input  A3,
  input  B3,
  input  C3,
  output Y1,
  output Y2,
  output Y3
);

  and and_1 (Y1, A1, B1, C1);
  and and_2 (Y2, A2, B2, C2);
  and and_3 (Y3, A3, B3, C3);
endmodule

module d_7410_3x3_input_NAND (
  input  A1,
  input  B1,
  input  C1,
  input  A2,
  input  B2,
  input  C2,
  input  A3,
  input  B3,
  input  C3,
  output Y1,
  output Y2,
  output Y3
);

  wire and_1_out, and_2_out, and_3_out;

  and and_1 (and_1_out, A1, B1, C1);
  and and_2 (and_2_out, A2, B2, C2);
  and and_3 (and_3_out, A3, B3, C3);
  not not_1 (Y1, and_1_out);
  not not_2 (Y2, and_2_out);
  not not_3 (Y3, and_3_out);
endmodule

module d_7420_2x4_input_NAND (
  input  A1,
  input  B1,
  input  C1,
  input  D1,
  input  A2,
  input  B2,
  input  C2,
  input  D2,
  output Y1,
  output Y2
);

  wire and_1_out, and_2_out;

  and and_1 (and_1_out, A1, B1, C1, D1);
  and and_2 (and_2_out, A2, B2, C2, D2);
  not not_1 (Y1, and_1_out);
  not not_2 (Y2, and_2_out);
endmodule
